# Fritzing sketch 4t45e interface module (saved by Fritzing 0.9.3b)
circuit board: 10cm x 7cm
breadboards: 2

parts:
  Q1 = Basic FET N-Channel [package="TO220 [THT]"]
  Q2 = Basic FET N-Channel [package="TO220 [THT]"]
  Q3 = Basic FET N-Channel [package="TO220 [THT]"]
  Q4 = Basic FET N-Channel [package="TO220 [THT]"]
  Q5 = Basic FET N-Channel [package="TO220 [THT]"]
  Q6 = Basic FET N-Channel [package="TO220 [THT]"]
  R1 = Resistor [tolerance=±5% resistance=330 package=THT]
  R2 = Resistor [tolerance=±5% resistance=330 package=THT]
  R3 = Resistor [tolerance=±5% resistance=330 package=THT]
  R4 = Resistor [tolerance=±5% resistance=330k package=THT]
  JP5 = Header 12 [package=1x12_machine-pin-header_lock.004]
  JP4 = Header 12 [package=1x12_machine-pin-header_lock.004]
  U1 = Voltage Regulator - 5V [package="TO220 [THT]"]

nets:
  N1: Q1.gate, JP4.3
  N2: Q1.drain, Q2.drain, Q3.drain, Q4.drain, Q5.source, Q6.source, JP4.2, JP4.12, U1.GND
  N3: Q1.source, R1.Pin_1, JP4.4
  N4: Q2.gate, JP4.5
  N5: Q2.source, R2.Pin_1, JP4.6
  N6: Q3.gate, JP4.7
  N7: Q3.source, R3.Pin_1, JP4.8
  N8: Q4.gate, JP4.9
  N9: Q4.source, R4.Pin_1, JP4.10
  N10: Q5.gate, JP5.4
  N11: Q5.drain, JP5.5
  N12: Q6.gate, JP5.2
  N13: Q6.drain, JP5.3
  N14: R1.Pin_0, R2.Pin_0, R3.Pin_0, R4.Pin_0, JP5.1
  N15: JP4.1, U1.input_voltage
  N16: JP4.11, U1.output_voltage

notes:
  TRS harness
  red is ground
  white is line +
  white jumpers to power resistors not on original breadboard - pin spacing on resistor won't edit???
  2017
